// Logisim project circuito.circ as structural Verilog: 1 circuit, main circuit main
module main (
  input  A,
  input  B,
  input  C,
  output out_4
);

  wire nand_1_out, nor_1_out, xor_1_out;

  nor nor_1 (nor_1_out, A, ~B, C);  // NOR_Gate
  nand nand_1 (nand_1_out, nor_1_out, ~B);  // NAND_Gate
  xor xor_1 (xor_1_out, nor_1_out, nand_1_out);
  not not_1 (out_4, xor_1_out);
endmodule
