// Logisim project circuito.circ as structural Verilog: 1 circuit, main circuit main
module main (
  input  A,
  input  B,
  input  C,
  output out_4
);

  wire and_1_out, and_2_out, and_3_out, or_1_out;

  and and_1 (and_1_out, ~A, B, ~C);  // AND_Gate
  or or_1 (or_1_out, ~and_1_out, B);  // OR_Gate
  and and_2 (and_2_out, and_1_out, or_1_out);
  and and_3 (and_3_out, ~and_1_out, ~or_1_out);  // AND_Gate
  or or_2 (out_4, and_2_out, and_3_out);
endmodule
