// Logisim project BatalhaNaval.circ as structural Verilog: 1 circuit, main circuit main
module main (
  input  A,
  input  B,
  input  C,
  input  D,
  input  E,
  input  F,
  input  G,
  input  H,
  input  A1,
  input  B1,
  input  C1,
  input  D1,
  input  in_13
);

  wire and_1_out, and_2_out, and_3_out, and_4_out, and_5_out, and_6_out, and_7_out, and_8_out, and_9_out,
       and_10_out, and_11_out, and_12_out, and_13_out, and_14_out, and_15_out, and_16_out, and_17_out,
       and_18_out, and_19_out, and_20_out, and_21_out, and_22_out, and_23_out, and_24_out, and_25_out,
       and_26_out, and_27_out, and_28_out, and_29_out, and_30_out, and_31_out, and_32_out, and_33_out,
       and_34_out, and_35_out, and_36_out, and_37_out, barco_1_out, barco_2_out, not_1_out, not_2_out,
       not_3_out, not_4_out, not_5_out, not_6_out, not_7_out, not_8_out, not_9_out, not_10_out, not_11_out,
       not_12_out, not_13_out, not_14_out, not_15_out, not_16_out, not_17_out, not_18_out, not_19_out,
       not_20_out, not_21_out, not_22_out, not_23_out, not_24_out, not_25_out, not_26_out, not_27_out,
       not_28_out, not_29_out, not_30_out, not_31_out, not_32_out, not_33_out, not_34_out, not_35_out,
       not_36_out, not_37_out, not_38_out, not_39_out, not_40_out, not_41_out, not_42_out, not_43_out,
       not_44_out, not_45_out, not_46_out, not_47_out, not_48_out, not_49_out, not_50_out, not_51_out,
       not_52_out, not_53_out, not_54_out, not_55_out, not_56_out, or_1_out, S1_2_out, S1_out, S2_2_out,
       S2_out, S3_2_out, S3_out, S4_2_out, S4_out, xnor_1_out, xnor_2_out, xnor_3_out, xnor_4_out,
       xnor_5_out, xnor_6_out, xnor_7_out, xnor_8_out;

  not not_1 (not_1_out, D);
  not not_2 (not_2_out, A);
  not not_3 (not_3_out, C);
  not not_4 (not_4_out, B);
  not not_5 (not_5_out, D);
  not not_6 (not_6_out, C);
  not not_7 (not_7_out, A);
  not not_8 (not_8_out, C);
  not not_9 (not_9_out, C);
  not not_10 (not_10_out, B);
  not not_11 (not_11_out, A);
  not not_12 (not_12_out, D);
  not not_13 (not_13_out, B);
  not not_14 (not_14_out, D);
  not not_15 (not_15_out, C);
  not not_16 (not_16_out, A);
  not not_17 (not_17_out, B);
  not not_18 (not_18_out, C);
  not not_19 (not_19_out, B);
  not not_20 (not_20_out, B);
  not not_21 (not_21_out, A);
  not not_22 (not_22_out, C);
  not not_23 (not_23_out, D);
  not not_24 (not_24_out, C);
  not not_25 (not_25_out, B);
  not not_26 (not_26_out, A);
  not not_27 (not_27_out, B);
  not not_28 (not_28_out, D);
  not not_29 (not_29_out, H);
  not not_30 (not_30_out, E);
  not not_31 (not_31_out, G);
  not not_32 (not_32_out, F);
  not not_33 (not_33_out, H);
  not not_34 (not_34_out, G);
  not not_35 (not_35_out, E);
  not not_36 (not_36_out, G);
  not not_37 (not_37_out, G);
  not not_38 (not_38_out, F);
  not not_39 (not_39_out, E);
  not not_40 (not_40_out, H);
  not not_41 (not_41_out, F);
  not not_42 (not_42_out, H);
  not not_43 (not_43_out, G);
  not not_44 (not_44_out, E);
  not not_45 (not_45_out, F);
  not not_46 (not_46_out, G);
  not not_47 (not_47_out, F);
  not not_48 (not_48_out, F);
  not not_49 (not_49_out, E);
  not not_50 (not_50_out, G);
  not not_51 (not_51_out, H);
  not not_52 (not_52_out, G);
  not not_53 (not_53_out, F);
  not not_54 (not_54_out, E);
  not not_55 (not_55_out, F);
  not not_56 (not_56_out, H);
  and and_1 (and_1_out, not_1_out, C, not_2_out);
  and and_2 (and_2_out, not_3_out, B, A);
  and and_3 (and_3_out, D, not_4_out);
  and and_4 (and_4_out, not_5_out, not_6_out, B, not_7_out);
  and and_5 (and_5_out, D, not_8_out, A);
  and and_6 (and_6_out, D, not_9_out, not_10_out);
  and and_7 (and_7_out, D, C, not_11_out);
  and and_8 (and_8_out, not_12_out, not_13_out, A);
  and and_9 (and_9_out, not_14_out, not_15_out, B, not_16_out);
  and and_10 (and_10_out, D, C, not_17_out);
  and and_11 (and_11_out, not_18_out, not_19_out, A);
  and and_12 (and_12_out, C, not_20_out, not_21_out);
  and and_13 (and_13_out, C, B, A);
  and and_14 (and_14_out, D, not_22_out, B, A);
  and and_15 (and_15_out, not_23_out, not_24_out, not_25_out);
  and and_16 (and_16_out, D, C, not_26_out);
  and and_17 (and_17_out, D, C, not_27_out);
  and and_18 (and_18_out, not_28_out, C, B);
  and and_19 (and_19_out, not_29_out, G, not_30_out);
  and and_20 (and_20_out, not_31_out, F, E);
  and and_21 (and_21_out, H, not_32_out);
  and and_22 (and_22_out, not_33_out, not_34_out, F, not_35_out);
  and and_23 (and_23_out, H, not_36_out, E);
  and and_24 (and_24_out, H, not_37_out, not_38_out);
  and and_25 (and_25_out, H, G, not_39_out);
  and and_26 (and_26_out, not_40_out, not_41_out, E);
  and and_27 (and_27_out, not_42_out, not_43_out, F, not_44_out);
  and and_28 (and_28_out, H, G, not_45_out);
  and and_29 (and_29_out, not_46_out, not_47_out, E);
  and and_30 (and_30_out, G, not_48_out, not_49_out);
  and and_31 (and_31_out, G, F, E);
  and and_32 (and_32_out, H, not_50_out, F, E);
  and and_33 (and_33_out, not_51_out, not_52_out, not_53_out);
  and and_34 (and_34_out, H, G, not_54_out);
  and and_35 (and_35_out, H, G, not_55_out);
  and and_36 (and_36_out, not_56_out, G, F);
  or S1 (S1_out, and_1_out, and_2_out, and_3_out);
  or S2 (S2_out, and_4_out, and_5_out, and_6_out, and_7_out, and_8_out);
  or S3 (S3_out, and_9_out, and_10_out, and_11_out, and_12_out, and_13_out);
  or S4 (S4_out, and_14_out, and_15_out, and_16_out, and_17_out, and_18_out);
  or S1_2 (S1_2_out, and_19_out, and_20_out, and_21_out);
  or S2_2 (S2_2_out, and_22_out, and_23_out, and_24_out, and_25_out, and_26_out);
  or S3_2 (S3_2_out, and_27_out, and_28_out, and_29_out, and_30_out, and_31_out);
  or S4_2 (S4_2_out, and_32_out, and_33_out, and_34_out, and_35_out, and_36_out);
  xnor xnor_1 (xnor_1_out, A1, S1_out);
  xnor xnor_2 (xnor_2_out, B1, S2_out);
  xnor xnor_3 (xnor_3_out, C1, S3_out);
  xnor xnor_4 (xnor_4_out, D1, S4_out);
  xnor xnor_5 (xnor_5_out, A1, S1_2_out);
  xnor xnor_6 (xnor_6_out, B1, S2_2_out);
  xnor xnor_7 (xnor_7_out, C1, S3_2_out);
  xnor xnor_8 (xnor_8_out, D1, S4_2_out);
  and barco_1 (barco_1_out, xnor_1_out, xnor_4_out);
  and barco_2 (barco_2_out, xnor_5_out, xnor_6_out, xnor_7_out, xnor_8_out);
  or or_1 (or_1_out, barco_1_out, barco_2_out);
  LED led_1 (.in(and_37_out));
  and and_37 (and_37_out, in_13, or_1_out, or_1_out);

  // Notes on the sheet:
  //   Entradas do usuario
endmodule
