// Logisim project circuito.circ as structural Verilog: 1 circuit, main circuit main
module main (
);

  wire and_1_out, and_2_out, and_3_out, and_4_out, and_5_out, and_6_out, and_7_out, and_8_out, and_9_out,
       and_10_out, and_11_out, and_12_out, and_13_out, and_14_out, and_15_out, and_16_out, clock_1_out,
       or_1_out, or_2_out, or_3_out, or_4_out, Q0_q, Q0_qn, Q1_q, Q1_qn, Q2_q, Q2_qn, Q3_q, Q3_qn;

  and and_1 (and_1_out, Q3_qn, Q2_qn, Q1_qn);
  and and_2 (and_2_out, Q3_qn, Q2_q, Q1_q);
  and and_3 (and_3_out, Q3_q, Q2_qn, Q1_q);
  and and_4 (and_4_out, Q3_q, Q2_q, Q1_qn);
  Clock clock_1 (.out(clock_1_out));
  and and_5 (and_5_out, Q1_q, Q2_q, Q3_q);
  and and_6 (and_6_out, Q1_qn, Q2_qn, Q3_q);
  and and_7 (and_7_out, Q1_qn, Q2_q, Q3_qn);
  and and_8 (and_8_out, Q1_q, Q2_qn, Q3_qn);
  or or_1 (or_1_out, and_1_out, and_2_out, and_3_out, and_4_out);
  J_K_Flip_Flop Q0 (.J(or_1_out), .K(or_2_out), .clk(clock_1_out), .Q(Q0_q), .Qn(Q0_qn));  // open: preset, reset
  or or_2 (or_2_out, and_5_out, and_6_out, and_7_out, and_8_out);
  and and_9 (and_9_out, Q2_qn, Q3_qn, Q0_q);
  and and_10 (and_10_out, Q3_q, Q2_q, Q0_q);
  and and_11 (and_11_out, Q0_q, Q2_qn, Q3_q);
  and and_12 (and_12_out, Q0_q, Q2_q, Q3_qn);
  or or_3 (or_3_out, and_9_out, and_10_out);
  J_K_Flip_Flop Q1 (.J(or_3_out), .K(or_4_out), .clk(clock_1_out), .Q(Q1_q), .Qn(Q1_qn));  // open: preset, reset
  or or_4 (or_4_out, and_11_out, and_12_out);
  and and_13 (and_13_out, Q3_qn, Q0_qn, Q1_q);
  and and_14 (and_14_out, Q0_qn, Q1_q, Q3_q);
  J_K_Flip_Flop Q2 (.J(and_13_out), .K(and_14_out), .clk(clock_1_out), .Q(Q2_q), .Qn(Q2_qn));  // open: preset, reset
  and and_15 (and_15_out, Q0_qn, Q1_qn, Q2_q);
  and and_16 (and_16_out, Q2_qn, Q1_qn, Q0_qn);
  J_K_Flip_Flop Q3 (.J(and_15_out), .K(and_16_out), .clk(clock_1_out), .Q(Q3_q), .Qn(Q3_qn));  // open: preset, reset
  LED led_1 (.in(Q3_q));
  LED led_2 (.in(Q2_q));
  LED led_3 (.in(Q1_q));
  LED led_4 (.in(Q0_q));
endmodule
