// Digital circuit maqRefrigerante(Digital).dig as structural Verilog
module maqRefrigerante_Digital (
  input  clk,
  input  in_2,
  input  in_3
);

  wire u_maqRefri_z;

  maqRefri #(.applicationType("GHDL")) u_maqRefri (.clock(clk), .reset(in_3), .w(in_2), .z(u_maqRefri_z));
  LED led_1 (.in(u_maqRefri_z));
endmodule

/* Code of maqRefri:
library ieee;
use ieee.std_logic_1164.all;

entity maqRefri is
    port(
        clock , reset , w : IN STD_LOGIC;
        z : OUT STD_LOGIC
        );
end maqRefri;

architecture Behavior OF maqRefri is
    type Tipo_estado is (A,B,C,D);
    signal y_atual, y_prox : Tipo_estado;
begin
    process (w, y_atual)
    begin
        case y_atual is
            when A =>
                if w = '0' then
                    y_prox <= B;
                else
                    y_prox <= C;
                end if;
            when B =>
                if w = '0' then
                    y_prox <= C;
                else
                    y_prox <= D;
                end if;
            when C =>
                if w = '0' then
                    y_prox <= D;
                else
                    y_prox <= D;
                end if;
             when D =>
                if w = '0' then
                    y_prox <= A;
                else
                    y_prox <= A;
                end if;
        end case;
    end process;

    process (clock, reset)
    begin
        if reset = '1' then
            y_atual <= A;
        elsif (clock'event and clock = '1') then
            y_atual <= y_prox;
        end if;
    end process;
    z <= '1' when y_atual = D else '0';
end Behavior;
*/
