// Logisim project maqRefrigerante(Logisim).circ as structural Verilog: 1 circuit, main circuit main
module main (
  input  w
);

  wire and_1_out, and_2_out, and_3_out, and_4_out, and_5_out, and_6_out, and_7_out, not_1_out, or_1_out,
       or_2_out, relogio_out, reset_out, y0_q, y0_qn, y1_q, y1_qn;

  and and_1 (and_1_out, y1_qn, y0_q);
  and and_2 (and_2_out, y1_q, y0_qn, w);
  and and_3 (and_3_out, y1_qn, not_1_out);
  not not_1 (not_1_out, w);
  and and_4 (and_4_out, w, y0_qn);
  and and_5 (and_5_out, y1_qn, y0_q);
  and and_6 (and_6_out, y1_q, y0_qn);
  or or_1 (or_1_out, and_1_out, and_2_out, and_3_out);
  Clock relogio (.out(relogio_out));
  or or_2 (or_2_out, and_4_out, and_5_out, and_6_out);
  Button reset (.out(reset_out));
  D_Flip_Flop y1 (.D(or_1_out), .clk(relogio_out), .Q(y1_q), .Qn(y1_qn), .reset(reset_out));  // open: preset
  D_Flip_Flop y0 (.D(or_2_out), .clk(relogio_out), .Q(y0_q), .Qn(y0_qn), .reset(reset_out));  // open: preset
  and and_7 (and_7_out, y1_q, y0_q);
  LED z (.in(and_7_out));
endmodule
